// Logisim project Udemy_design_a_cpu.circ as structural Verilog: 9 circuits, main circuit main
module main (
  input  [7:0] i,
  input  s,
  input  e,
  output [7:0] o
);

  wire [7:0] cpu_mem_8_1_o;

  CPU_MEM_8 cpu_mem_8_1 (.o(cpu_mem_8_1_o), .s(s), .in_1(i));
  CPU_ENABLE cpu_enable_1 (.i(cpu_mem_8_1_o), .o(o), .e(e));
endmodule

module \nand  (
  input  a,
  input  b,
  output O
);

  wire and_1_out;

  and and_1 (and_1_out, a, b);
  not not_1 (O, and_1_out);
endmodule

module C1 (
  input  [7:0] i,
  output o
);

  wire nand_1_o, nand_2_o, nand_3_o, nand_4_o, undriven_2, undriven_3, undriven_4, undriven_5, undriven_6,
       undriven_7;
  wire [1:0] undriven;

  \nand  nand_1 (.a(undriven[0]), .b(undriven[1]), .O(nand_1_o));
  \nand  nand_2 (.a(undriven_2), .b(undriven_3), .O(nand_2_o));
  \nand  nand_3 (.a(undriven_4), .b(undriven_5), .O(nand_3_o));
  \nand  nand_4 (.a(undriven_6), .b(undriven_7), .O(nand_4_o));
  nor nor_1 (o, nand_1_o, nand_2_o, nand_3_o, nand_4_o);
endmodule

module C_Map1 (
  input  in_1,
  input  in_2,
  input  in_3,
  input  in_4,
  input  in_5,
  input  in_6,
  input  in_7,
  input  in_8,
  input  in_9,
  output out_10,
  output out_11,
  output out_12,
  output out_13,
  output out_14
);

  wire nand_1_out, nand_2_out, nand_3_out, nand_4_out, nand_5_out, nand_9_out;

  nand nand_1 (nand_1_out, in_4, in_5);
  nand nand_2 (nand_2_out, in_6, in_6);
  nand nand_3 (nand_3_out, in_7, in_7);
  nand nand_4 (nand_4_out, in_8, in_8);
  nand nand_5 (nand_5_out, in_9, in_9);
  nand nand_6 (out_10, in_1, in_2);
  nand nand_7 (out_11, in_3, in_3);
  nand nand_8 (out_12, nand_1_out, nand_1_out);
  nand nand_9 (nand_9_out, nand_4_out, nand_5_out);
  nand nand_10 (out_13, nand_2_out, nand_3_out);
  not not_1 (out_14, nand_9_out);

  // Notes on the sheet:
  //   OR
  //   NOT
  //   NOT
  //   NOR
  //   NOT
  //   NOT
  //   NAND
  //   NOT
  //   AND
endmodule

module C_Map_2 (
  input  in_1,
  input  in_2,
  input  in_3,
  input  in_4,
  output out_5,
  output out_6
);

  wire nand_1_out, nand_2_out, nand_3_out, nand_4_out, nand_6_out, not_1_out, not_2_out, not_3_out, not_4_out;

  not not_1 (not_1_out, in_1);
  not not_2 (not_2_out, in_2);
  not not_3 (not_3_out, in_3);
  not not_4 (not_4_out, in_4);
  nand nand_1 (nand_1_out, not_1_out, in_2);
  nand nand_2 (nand_2_out, in_1, not_2_out);
  nand nand_3 (nand_3_out, not_3_out, in_4);
  nand nand_4 (nand_4_out, in_3, not_4_out);
  nand nand_5 (out_5, nand_1_out, nand_2_out);
  not not_5 (out_6, nand_6_out);
  nand nand_6 (nand_6_out, nand_3_out, nand_4_out);

  // Notes on the sheet:
  //   XOR
  //   XNOR
  //   0 1 1 0
  //   1 0 0 1
endmodule

module CPU_MEM_1 (
  input  s,
  input  e,
  output q
);

  wire nand_1_out, nand_2_out, nand_4_out;

  nand nand_1 (nand_1_out, s, e);
  nand nand_2 (nand_2_out, nand_1_out, e);
  nand nand_3 (q, nand_1_out, nand_4_out);
  nand nand_4 (nand_4_out, q, nand_2_out);

  // Notes on the sheet:
  //   1 bit memory cell
endmodule

module CPU_MEM_8 (
  input  [7:0] in_1,
  input  s,
  output [7:0] o
);

  CPU_MEM_1 cpu_mem_1_1 (.s(in_1[0]), .e(s), .q(o[0]));
  CPU_MEM_1 cpu_mem_1_2 (.s(in_1[1]), .e(s), .q(o[1]));
  CPU_MEM_1 cpu_mem_1_3 (.s(in_1[2]), .e(s), .q(o[2]));
  CPU_MEM_1 cpu_mem_1_4 (.s(in_1[3]), .e(s), .q(o[3]));
  CPU_MEM_1 cpu_mem_1_5 (.s(in_1[4]), .e(s), .q(o[4]));
  CPU_MEM_1 cpu_mem_1_6 (.s(in_1[5]), .e(s), .q(o[5]));
  CPU_MEM_1 cpu_mem_1_7 (.s(in_1[6]), .e(s), .q(o[6]));
  CPU_MEM_1 cpu_mem_1_8 (.s(in_1[7]), .e(s), .q(o[7]));
endmodule

module CPU_ENABLE (
  input  [7:0] i,
  input  e,
  output [7:0] o
);

  and and_1 (o[0], i[0], e);
  and and_2 (o[1], i[1], e);
  and and_3 (o[2], i[2], e);
  and and_4 (o[3], i[3], e);
  and and_5 (o[4], i[4], e);
  and and_6 (o[5], i[5], e);
  and and_7 (o[6], i[6], e);
  and and_8 (o[7], i[7], e);
endmodule

module CPU_REG_8 (
  input  [7:0] i,
  input  s,
  input  e,
  output [7:0] o
);

  wire [7:0] cpu_mem_8_1_o;

  CPU_MEM_8 cpu_mem_8_1 (.o(cpu_mem_8_1_o), .s(s), .in_1(i));
  CPU_ENABLE cpu_enable_1 (.i(cpu_mem_8_1_o), .o(o), .e(e));
endmodule
